// Logisim project RISC 32 BIT MAIN.circ as structural Verilog: 1 circuit, main circuit main
module main (
);

  wire clock_1_out;
  wire [31:0] Input, OP1, OP2, Result;

  Clock clock_1 (.out(clock_1_out));
  RISC_32_BIT_ALU_main main_1 (
    .Clock(clock_1_out), .Result(Result), .OP1(OP1), .OP2(OP2));  // open: OpeartionCode, in_1
  // RISC_32_BIT_REGISTERS_main main_2: pin names not known; wires that end beside it: Input, clock_1_out, OP1, OP2
endmodule
